// Digital circuit Prob 3 Mean.dig as structural Verilog
module Prob_3_Mean (
  input  [15:0] A,
  input  \input ,
  input  reset,
  input  clk,
  output [15:0] mean,
  output busy
);

  wire comparator_1_gt, d_ff_1_q, d_ff_2_q, d_ff_3_nq, or_1_out, or_2_out;
  wire [15:0] A_t, add_1_s, add_2_s, count, div_1_q, multiplexer_1_out, multiplexer_2_out, multiplexer_3_out;
  wire [31:0] mul_1_mul;

  or or_1 (or_1_out, \input , reset);
  Multiplexer #(.Bits(16)) multiplexer_1 (.sel(reset), .in_0(A), .in_1({16{1'b0}}), .out(multiplexer_1_out));
  Register #(.Bits(16)) u_A (.D(multiplexer_1_out), .C(clk), .en(or_1_out), .Q(A_t));
  Mul #(.Bits(16)) mul_1 (.a(mean), .b(count), .mul(mul_1_mul));
  Add #(.Bits(16)) add_1 (.a(mul_1_mul[15:0]), .b(A_t), .c_i(1'b0), .s(add_1_s));  // open: c_o
  Add #(.Bits(16)) add_2 (.a(count), .b(16'h1), .c_i(1'b0), .s(add_2_s));  // open: c_o
  Multiplexer #(.Bits(16)) multiplexer_2 (.sel(reset), .in_0(add_2_s), .in_1({16{1'b0}}), .out(multiplexer_2_out));
  Register #(.Bits(16)) u_Count (.D(multiplexer_2_out), .C(clk), .en(busy), .Q(count));
  Div #(.Bits(16)) div_1 (.a(add_1_s), .b(add_2_s), .q(div_1_q));  // open: r
  Multiplexer #(.Bits(16)) multiplexer_3 (.sel(reset), .in_0(div_1_q), .in_1({16{1'b0}}), .out(multiplexer_3_out));
  Comparator #(.Bits(16)) comparator_1 (.a(div_1_q), .b(mean), .gt(comparator_1_gt));  // open: eq, lt
  Register #(.Bits(16)) u_Mean (.D(multiplexer_3_out), .C(clk), .en(busy), .Q(mean));
  and and_1 (busy, d_ff_2_q, d_ff_1_q);
  D_FF d_ff_1 (.D(or_2_out), .C(clk), .Q(d_ff_1_q));  // open: nQ
  D_FF d_ff_2 (.D(d_ff_3_nq), .C(clk), .Q(d_ff_2_q));  // open: nQ
  D_FF d_ff_3 (.D(or_2_out), .C(clk), .nQ(d_ff_3_nq));  // open: Q
  or or_2 (or_2_out, comparator_1_gt, reset);
endmodule
